# Fritzing sketch aquarium (saved by Fritzing 0.9.1b)
circuit board: 8.46667cm x 5.64444cm
breadboards: 1

parts:
  Tiny_RTC = Tiny RTC
  S5 = Pushbutton [package="[THT]"]
  S4 = Pushbutton [package="[THT]"]
  S3 = Pushbutton [package="[THT]"]
  S2 = Pushbutton [package="[THT]"]
  S1 = Pushbutton [package="[THT]"]
  R7 = Resistor [tolerance=±5% resistance=2.2k package=THT]
  R6 = Resistor [tolerance=±5% resistance=1k package=THT]
  R5 = Resistor [tolerance=±5% resistance=680 package=THT]
  R4 = Resistor [tolerance=±5% resistance=330 package=THT]
  R3 = Resistor [tolerance=±5% resistance=2k package=THT]
  LED2 = LED - 5mm [color="Red (633nm)" package="5 mm [THT]"]
  LED3 = LED - 5mm [color="Yellow (585nm)" package="5 mm [THT]"]
  LED4 = LED - 5mm [color="Green (555nm)" package="5 mm [THT]"]
  LED5 = LED - 5mm [color="Blue (470nm)" package="5 mm [THT]"]
  R11 = Resistor [tolerance=±5% resistance=220 package=THT]
  R12 = Resistor [tolerance=±5% resistance=220 package=THT]
  R13 = Resistor [tolerance=±5% resistance=220 package=THT]
  R14 = Resistor [tolerance=±5% resistance=220 package=THT]
  LED1 = LED - 5mm [color="Green (570nm)" package="5 mm [THT]"]
  R15 = Resistor [tolerance=±5% resistance=220 package=THT]
  J1_-_18V = Power Jack [package=power_jack_smd]
  Power_LED9 = Power LED on star
  Power_LED4 = Power LED on star
  Power_LED1 = Power LED on star
  Power_LED7 = Power LED on star
  Power_LED6 = Power LED on star
  Power_LED3 = Power LED on star
  Power_LED5 = Power LED on star
  Power_LED2 = Power LED on star
  Power_LED8 = Power LED on star
  LDD-1000H1 = MeanWell LDD-1000H
  LDD-1000H2 = MeanWell LDD-1000H
  4_Relay_Module1 = 4 Relay Module
  Part2 = Arduino Pro Mini v13
  WF_S1 = WaterFlow hall effect sensor [part_number=toto]  # not connected
  DS1 = DS18B20 1-Wire Temperature Sensor [part_number=DS18B20]  # not connected
  Part1 = QSKJ DC-DC stepdown converter
  I2C_LCD1 = LCD screen witch I2C connector

nets:
  N1: Tiny_RTC.SCL, Part2.A5
  N2: Tiny_RTC.SDA, Part2.A4
  5V: Tiny_RTC.VCC, R3.Pin_0, 4_Relay_Module1.VCC, 4_Relay_Module1.IN4, Part2.VCC, Part1.OUT+
  GND: Tiny_RTC.GND, S5.Pin_1, S5.Pin_2, S4.Pin_1, S4.Pin_2, S3.Pin_1, S3.Pin_2, S2.Pin_1, S2.Pin_2, S1.Pin_1, S1.Pin_2, R11.Pin_0, R12.Pin_0, R13.Pin_0, R14.Pin_0, R15.Pin_0, 4_Relay_Module1.GND, Part2.GND, Part1.OUT-, I2C_LCD1.GND
  N3: S5.Pin_3, S5.Pin_4, R7.Pin_1
  N4: S4.Pin_3, S4.Pin_4, R7.Pin_0, R6.Pin_1
  N5: S3.Pin_3, S3.Pin_4, R6.Pin_0, R5.Pin_1
  N6: S2.Pin_3, S2.Pin_4, R5.Pin_0, R4.Pin_1
  N7: S1.Pin_3, S1.Pin_4, R4.Pin_0, R3.Pin_1, Part2.A1
  N8: LED2.cathode, R11.Pin_1
  Light_1: LED2.anode, LDD-1000H1.PWM_DIM, Part2.D10_PWM/SS
  N9: LED3.cathode, R12.Pin_1
  N10: LED3.anode, Part2.D11_PWM/MOSI
  N11: LED4.cathode, R13.Pin_1
  Switch_1: LED4.anode, 4_Relay_Module1.IN1, Part2.D9_PWM
  N12: LED5.cathode, R14.Pin_1
  Switch_2: LED5.anode, 4_Relay_Module1.IN2, Part2.D8
  N13: LED1.cathode, R15.Pin_1
  N14: LED1.anode, Part2.D7
  N15: J1_-_18V.PWR, LDD-1000H1.+Vin, LDD-1000H2.+Vin, Part1.IN+
  N16: J1_-_18V.GND, LDD-1000H1.-Vin, LDD-1000H2.-Vin, Part1.IN-
  N17: Power_LED9.+, Power_LED8.-
  N18: Power_LED9.-, LDD-1000H2.-Vout
  N19: Power_LED4.+, Power_LED3.-
  N20: Power_LED4.-, LDD-1000H1.-Vout
  N21: Power_LED1.+, LDD-1000H1.+Vout
  N22: Power_LED1.-, Power_LED2.+
  N23: Power_LED7.+, Power_LED6.-
  N24: Power_LED7.-, Power_LED8.+
  N25: Power_LED6.+, Power_LED5.-
  N26: Power_LED3.+, Power_LED2.-
  N27: Power_LED5.+, LDD-1000H2.+Vout
  Light_2: LDD-1000H2.PWM_DIM

notes:
  Light_1
  Light_2
  Switch_1
  Switch_2

custom parts:
  Tiny RTC: Tiny RTC I2C module DS1370Z RTC and AT24C32 EEPROM
  Power LED on star: PCB mounted RGB LED.
  MeanWell LDD-1000H: DC-DC Constant Current Step-Down LED drive
  4 Relay Module: a 4 relay module for Arduino or other
  DS18B20 1-Wire Temperature Sensor: DS18B20 1-Wire Temperature Sensor - waterproof version
  QSKJ DC-DC stepdown converter: Description: This is a 2A stepdown converter - Brand: Jtron - Model: 03100125 - Color: Red - Material: Glass fiber - Module properties: Non-isolated step-down module (Buck) - Rectification: Non-synchronous - Input voltage: DC 4.5~35V - Output voltage: 1.25~30V (adjustable or fixed) - Rated current: 2A - Output current: Max. 3A; Suggest add heat sink if output power is over 15W - Conversion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
  LCD screen witch I2C connector: A standard character display with I2C interface, usually with 2x16 characters. Comes in many colors.
